# Fritzing sketch Plant_Monitoring_Project_v1.0 (saved by Fritzing 0.9.3b)
breadboards: 1

parts:
  Part1 = Arduino Pro Mini (3.3V)
  Part3 = Adafruit TSL2591 [part_number="Adafruit #1980"]
  Capacitive_Soil_Moisture_Sensor1 = DFRobot Capacitive Soil Moisture Sensor V1.0 [part_number=SEN0193]
  Part4 = NRF24L01+ Breakout Board
  DHT1 = DHT22 Humidity and Temperature Sensor
  DS1 = DS18B20 1-Wire Temperature Sensor Probe Cable

nets:
  VCC: Part1.VCC, Part3.VIN, Capacitive_Soil_Moisture_Sensor1.VCC, Part4.VCC, DHT1.VDD, DS1.VDD
  GND: Part1.GND, Part3.GND, Capacitive_Soil_Moisture_Sensor1.GND, Part4.GND, DHT1.GND, DS1.GND
  N1: Part1.A4, Part3.SDA
  N2: Part1.A5, Part3.SCL
  N3: Part1.A0, Capacitive_Soil_Moisture_Sensor1.A
  N4: Part1.SCK, Part4.SCK
  N5: Part1.MISO, Part4.MISO
  N6: Part1.MOSI, Part4.MOSI
  N7: Part1.D10, Part4.CS
  N8: Part1.D9, Part4.CE
  N9: Part1.D3, DS1.shield
  N10: Part1.D2, DHT1.DATA

custom parts:
  Adafruit TSL2591: When the future is dazzlingly-bright, this ultra-high-range luminosity sensor will help you measure it. The TSL2591 luminosity sensor is an advanced digital light sensor, ideal for use in a wide range of light situations. Compared to low cost CdS cells, this sensor is more precise, allowing for exact lux calculations and can be configured for different gain/timing ranges to detect light ranges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
  DFRobot Capacitive Soil Moisture Sensor V1.0: DFRobot Capacitive Soil Moisture Sensor V1.0 This product measures soil moisture levels by capacitive sensing, rather than resistive sensing like other types of moisture sensor. It is made of a corrosion resistant material giving it a long service life. Insert it into soil and impress your friends with the real-time soil moisture data! The product includes an on-board voltage regulator which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
